// Logisim project H2.circ as structural Verilog
module P2 (
  input  S1,
  input  S0,
  input  In,
  output S1n,
  output S0n,
  output Out
);

  wire and_1_out, and_2_out, and_3_out, and_4_out, and_5_out, and_7_out, and_8_out, not_1_out, not_2_out,
       not_3_out;

  not not_1 (not_1_out, S1);
  not not_2 (not_2_out, In);
  not not_3 (not_3_out, S0);
  and and_1 (and_1_out, not_1_out, not_3_out, not_2_out);
  and and_2 (and_2_out, not_1_out, not_3_out, In);
  and and_3 (and_3_out, not_1_out, S0, not_2_out);
  and and_4 (and_4_out, not_1_out, S0, In);
  and and_5 (and_5_out, S1, not_3_out, not_2_out);
  // AND_Gate and_6 has open pins: in0=S1, in1=not_3_out, in2=In, out=open
  and and_7 (and_7_out, S1, S0, not_2_out);
  and and_8 (and_8_out, S1, S0, In);
  or or_1 (S1n, and_1_out, and_5_out, and_7_out);
  or or_2 (S0n, and_2_out, and_4_out, and_5_out);
  or or_3 (Out, and_2_out, and_3_out, and_5_out, and_7_out, and_8_out);

  // Notes on the sheet:
  //   PROBLEM 2: IMPLEMENTING A STATE TABLE
  //   INPUT SECTION: Do not change anything here!
  //   You may only change the values of the inputs for testing using the hand tool.
  //   Do not introduce any other input or output pins in the circuit.
  //   To your logic
  //   OUTPUT SECTION: Do not change anything here!
  //   Do not introduce any other input or output pins in the circuit.
  //   From your logic
endmodule

module P3 (
  input  In,
  output Out
);

  wire and_2_out, and_3_out, and_4_out, and_5_out, and_6_out, and_7_out, and_8_out, and_9_out, and_10_out,
       not_1_out, not_2_out, not_3_out, not_4_out, not_5_out, not_6_out, not_7_out, not_8_out, not_9_out,
       not_10_out, not_11_out, not_12_out, or_1_out, or_2_out, or_3_out;

  and and_1 (Out, or_1_out, or_2_out);
  not not_1 (not_1_out, or_1_out);
  not not_2 (not_2_out, or_2_out);
  not not_3 (not_3_out, In);
  not not_4 (not_4_out, In);
  not not_5 (not_5_out, In);
  not not_6 (not_6_out, or_2_out);
  not not_7 (not_7_out, or_3_out);
  not not_8 (not_8_out, In);
  not not_9 (not_9_out, or_2_out);
  not not_10 (not_10_out, or_1_out);
  not not_11 (not_11_out, or_3_out);
  not not_12 (not_12_out, In);
  and and_2 (and_2_out, not_1_out, not_2_out, not_3_out);
  and and_3 (and_3_out, or_3_out, not_4_out);
  and and_4 (and_4_out, or_2_out, or_3_out);
  and and_5 (and_5_out, or_1_out, or_2_out, not_5_out);
  and and_6 (and_6_out, or_2_out, or_3_out, In);
  and and_7 (and_7_out, or_1_out, not_6_out, not_7_out, not_8_out);
  and and_8 (and_8_out, or_1_out, or_3_out, In);
  and and_9 (and_9_out, not_9_out, or_3_out);
  and and_10 (and_10_out, not_10_out, or_2_out, not_11_out, not_12_out);
  or or_1 (or_1_out, and_2_out, and_3_out, and_4_out, and_5_out);
  or or_2 (or_2_out, and_6_out, and_7_out, and_8_out);
  or or_3 (or_3_out, and_9_out, and_10_out);

  // Notes on the sheet:
  //   PROBLEM 3: IMPLEMENTING A STATE MACHINE
  //   INPUT SECTION: Do not change anything here!
  //   You may only change the values of the inputs for testing using the hand tool.
  //   Do not introduce any other input or output pins in the circuit.
  //   To your logic
  //   OUTPUT SECTION: Do not change anything here!
  //   Do not introduce any other input or output pins in the circuit.
  //   From your logic
endmodule
