// Logisim project car alarm.circ as structural Verilog: 1 circuit, main circuit main
module main (
  input  M,
  input  V,
  input  D,
  output out_4
);

  wire and_1_out, and_2_out, and_3_out, clock_1_out, d_ff_1_q, undriven, undriven_2;

  and and_1 (and_1_out, out_4, M);
  and and_2 (and_2_out, M, V);
  and and_3 (and_3_out, M, D);
  Clock clock_1 (.out(clock_1_out));
  or or_1 (out_4, and_1_out, and_2_out, and_3_out);
  D_Flip_Flop d_ff_1 (.clk(undriven), .D(undriven_2), .Q(d_ff_1_q));  // open: Qn, preset, en, reset
endmodule
